// Logisim project HW4.circ as structural Verilog: 19 circuits, main circuit main
module main (
  input  in_1
);

  wire and_1_out, and_2_out, bneblehandler_1_bneble_out, clock_1_out, cu_1_alu_src, cu_1_bne_or_ble,
       cu_1_branchout, cu_1_call_out, cu_1_halt_out, cu_1_jump_out, cu_1_mem_read, cu_1_mem_to_reg,
       cu_1_mem_write, cu_1_move_out, cu_1_reg_dst, cu_1_reg_write, cu_1_rtn_out, not_1_out;
  wire [1:0] cu_1_alu_op;
  wire [2:0] multiplexer_4_out, multiplexer_6_out;
  wire [5:0] multiplexer_5_out;
  wire [15:0] adder_1_out, adder_2_out, alu_1_alu_out, bit_extender_1_out, multiplexer_1_out,
       multiplexer_2_out, multiplexer_3_out, multiplexer_7_out, multiplexer_8_out, multiplexer_9_out,
       multiplexer_10_out, multiplexer_11_out, multiplexer_12_out, multiplexer_13_out, PC_q, ra_q,
       ram_1_dout, register_file_1_d1, register_file_1_d2, rom_1_data, shifter_1_out;

  Clock clock_1 (.out(clock_1_out));
  Register #(.width(16)) ra (.D(multiplexer_1_out), .en(1'b1), .Q(ra_q), .clk(and_1_out));  // open: clr
  not not_1 (not_1_out, cu_1_halt_out);
  and and_1 (and_1_out, not_1_out, clock_1_out);
  Multiplexer #(.enable("true"), .width(16)) multiplexer_1 (
    .in0(ra_q), .in1(adder_1_out), .out(multiplexer_1_out), .sel(cu_1_call_out));  // open: en
  Multiplexer #(.enable("true"), .width(16)) multiplexer_2 (
    .in0(multiplexer_12_out), .in1(ra_q), .out(multiplexer_2_out), .sel(cu_1_rtn_out));  // open: en
  Register #(.width(16)) PC (.D(multiplexer_2_out), .en(1'b1), .Q(PC_q), .clk(and_1_out));  // open: clr
  Adder #(.width(16)) adder_1 (.a(16'h1), .b(PC_q), .out(adder_1_out));  // open: cin, cout
  ROM #(.addrWidth(16), .dataWidth(16)) rom_1 (.addr(PC_q), .data(rom_1_data));
  Multiplexer #(.enable("true"), .width(16)) multiplexer_3 (
    .in0(adder_1_out), .in1(PC_q), .out(multiplexer_3_out), .sel(cu_1_jump_out));  // open: en
  CU cu_1 (
    .in_1(rom_1_data[14:11]), .move_out(cu_1_move_out), .Reg_Dst(cu_1_reg_dst), .BranchOut(cu_1_branchout),
    .Mem_Read(cu_1_mem_read), .Mem_To_Reg(cu_1_mem_to_reg), .ALU_Op(cu_1_alu_op), .Mem_Write(cu_1_mem_write),
    .ALU_Src(cu_1_alu_src), .Reg_Write(cu_1_reg_write), .bne_or_ble(cu_1_bne_or_ble),
    .Halt_Out(cu_1_halt_out), .Jump_out(cu_1_jump_out), .Call_out(cu_1_call_out), .rtn_out(cu_1_rtn_out));
  Multiplexer #(.enable("true"), .width(3)) multiplexer_4 (
    .in0(rom_1_data[7:5]), .in1(rom_1_data[4:2]), .out(multiplexer_4_out), .sel(in_1));  // open: en
  Multiplexer #(.enable("true"), .width(6)) multiplexer_5 (
    .in0({rom_1_data[15], rom_1_data[10:8], rom_1_data[1:0]}), .in1({rom_1_data[15], rom_1_data[4:0]}),
    .out(multiplexer_5_out), .sel(cu_1_branchout));  // open: en
  Multiplexer #(.enable("true"), .width(3)) multiplexer_6 (
    .in0(multiplexer_4_out), .in1(rom_1_data[10:8]), .out(multiplexer_6_out), .sel(cu_1_move_out));  // open: en
  assign bit_extender_1_out = {{10{multiplexer_5_out[5]}}, multiplexer_5_out};  // Bit_Extender bit_extender_1
  Register_File register_file_1 (
    .W(cu_1_reg_write), .read2(rom_1_data[10:8]), .read1(rom_1_data[7:5]), .reg_W(multiplexer_6_out),
    .d_W(multiplexer_13_out), .clk(and_1_out), .d1(register_file_1_d1), .d2(register_file_1_d2));  // open: reset
  // Probe on register_file_1_d1
  // Probe on register_file_1_d2
  Multiplexer #(.enable("true"), .width(16)) multiplexer_7 (
    .in0(register_file_1_d2), .in1(bit_extender_1_out), .out(multiplexer_7_out), .sel(cu_1_alu_src));  // open: en
  Shifter #(.width(16)) shifter_1 (.in(bit_extender_1_out), .\dist (4'b0001), .out(shifter_1_out));
  Multiplexer #(.enable("true"), .width(16)) multiplexer_8 (
    .in0(alu_1_alu_out), .in1(register_file_1_d1), .out(multiplexer_8_out), .sel(cu_1_move_out));  // open: en
  Multiplexer #(.enable("true"), .width(16)) multiplexer_9 (
    .in0(shifter_1_out), .in1(bit_extender_1_out), .out(multiplexer_9_out), .sel(cu_1_jump_out));  // open: en
  ALU alu_1 (.A(register_file_1_d1), .B(multiplexer_7_out), .ALU_Op(cu_1_alu_op), .ALU_out(alu_1_alu_out));
  Adder #(.width(16)) adder_2 (.a(multiplexer_3_out), .b(multiplexer_9_out), .out(adder_2_out));  // open: cin, cout
  and and_2 (and_2_out, cu_1_branchout, bneblehandler_1_bneble_out);
  RAM #(.addrWidth(16), .dataWidth(16), .trigger("falling")) ram_1 (
    .addr(register_file_1_d2), .we(cu_1_mem_write), .oe(cu_1_mem_read), .clk(and_1_out),
    .din(register_file_1_d1), .dout(ram_1_dout));
  BneBleHandler bneblehandler_1 (
    .input1(register_file_1_d1), .input2(register_file_1_d2), .bne_ble_state_1bne_0ble(cu_1_bne_or_ble),
    .BNEBLE_out(bneblehandler_1_bneble_out));
  Multiplexer #(.enable("true"), .width(16)) multiplexer_10 (
    .in0(multiplexer_3_out), .in1(adder_2_out), .out(multiplexer_10_out), .sel(cu_1_jump_out));  // open: en
  Multiplexer #(.enable("true"), .width(16)) multiplexer_11 (
    .in0(multiplexer_3_out), .in1(adder_2_out), .out(multiplexer_11_out), .sel(and_2_out));  // open: en
  // Probe on multiplexer_3_out
  Multiplexer #(.enable("true"), .width(16)) multiplexer_12 (
    .in0(multiplexer_11_out), .in1(multiplexer_10_out), .out(multiplexer_12_out), .sel(cu_1_jump_out));  // open: en
  // Probe on ram_1_dout
  Multiplexer #(.enable("true"), .width(16)) multiplexer_13 (
    .in0(multiplexer_8_out), .in1(ram_1_dout), .out(multiplexer_13_out), .sel(cu_1_mem_to_reg));  // open: en
  // Probe on multiplexer_13_out

  // Notes on the sheet:
  //   contents of rom_1 (hex, n*v repeats v):
  //   ffff 7902 7905 6908 781c 5740 610c 781d 5760 781d 5f18
endmodule

module ALU (
  input  [15:0] A,
  input  [15:0] B,
  input  [1:0] ALU_Op,
  output [15:0] ALU_out
);

  wire [15:0] adder_1_out, and_1_out, or_1_out;

  Adder #(.width(16)) adder_1 (.a(A), .b(B), .out(adder_1_out));  // open: cin, cout
  assign and_1_out = A & B;  // AND_Gate and_1, 16 bits wide
  assign or_1_out = A | B;  // OR_Gate or_1, 16 bits wide
  Multiplexer #(.enable("true"), .select(2), .width(16)) multiplexer_1 (
    .in0(adder_1_out), .in1(B), .in2(and_1_out), .in3(or_1_out), .out(ALU_out), .sel(ALU_Op), .en(1'b1));
endmodule

module CU (
  input  [3:0] in_1,
  output Reg_Dst,
  output BranchOut,
  output Mem_Read,
  output Mem_To_Reg,
  output [1:0] ALU_Op,
  output Mem_Write,
  output ALU_Src,
  output Reg_Write,
  output bne_or_ble,
  output Halt_Out,
  output Jump_out,
  output Call_out,
  output rtn_out,
  output move_out
);

  RegDst regdst_1 (.OpCode(in_1), .Reg_Dst(Reg_Dst));
  Branch branch_1 (.OpCode(in_1), .Branch_Out(BranchOut));
  MemRead memread_1 (.OpCode(in_1), .Mem_Read(Mem_Read));
  MemToReg memtoreg_1 (.OpCode(in_1), .Mem_To_Reg(Mem_To_Reg));
  ALUOp aluop_1 (.OpCode(in_1), .ALU_Op(ALU_Op));
  MemWrite memwrite_1 (.OpCode(in_1), .Mem_Write(Mem_Write));
  ALUSrc alusrc_1 (.OpCode(in_1), .ALU_Src(ALU_Src));
  RegWrite regwrite_1 (.OpCode(in_1), .Reg_Write(Reg_Write));
  bne bne_1 (.in_1(in_1), .bne_out(bne_or_ble));
  Halt halt_1 (.in_1(in_1), .Halt_Out(Halt_Out));
  Jump jump_1 (.OpCode(in_1), .Jump_out(Jump_out));
  Call call_1 (.in_1(in_1), .call_out(Call_out));
  Rtn rtn_1 (.in_1(in_1), .rtn_out(rtn_out));
  Move move_1 (.in_1(in_1), .move_out(move_out));
endmodule

module RegDst (
  input  [3:0] OpCode,
  output Reg_Dst
);

  wire and_1_out, not_1_out;

  not not_1 (not_1_out, OpCode[0]);
  and and_1 (and_1_out, OpCode[3], not_1_out);
  or or_1 (Reg_Dst, and_1_out, OpCode[2]);
endmodule

module ALUSrc (
  input  [3:0] OpCode,
  output ALU_Src
);

  wire and_1_out, and_2_out, and_3_out, and_4_out, and_5_out, and_6_out, not_1_out, not_2_out, not_3_out,
       or_1_out;

  not not_1 (not_1_out, OpCode[3]);
  and and_1 (and_1_out, not_1_out, OpCode[2]);
  and and_2 (and_2_out, OpCode[3], not_2_out);
  not not_2 (not_2_out, OpCode[2]);
  and and_3 (and_3_out, OpCode[3], OpCode[1]);
  and and_4 (and_4_out, and_1_out, OpCode[1]);
  and and_5 (and_5_out, and_2_out, not_3_out);
  not not_3 (not_3_out, OpCode[0]);
  and and_6 (and_6_out, and_3_out, OpCode[0]);
  or or_1 (or_1_out, and_4_out, and_5_out);
  or or_2 (ALU_Src, or_1_out, and_6_out);
endmodule

module MemToReg (
  input  [3:0] OpCode,
  output Mem_To_Reg
);

  wire and_1_out, and_2_out, not_1_out;

  and and_1 (and_1_out, OpCode[3], not_1_out);
  not not_1 (not_1_out, OpCode[2]);
  and and_2 (and_2_out, and_1_out, OpCode[1]);
  and and_3 (Mem_To_Reg, and_2_out, OpCode[0]);
endmodule

module RegWrite (
  input  [3:0] OpCode,
  output Reg_Write
);

  wire and_1_out, and_2_out, and_3_out, not_1_out, or_1_out;

  and and_1 (and_1_out, OpCode[3], not_1_out);
  not not_1 (not_1_out, OpCode[1]);
  and and_2 (and_2_out, OpCode[2], OpCode[1]);
  and and_3 (and_3_out, OpCode[3], OpCode[0]);
  or or_1 (or_1_out, and_1_out, and_2_out);
  or or_2 (Reg_Write, or_1_out, and_3_out);
endmodule

module MemRead (
  input  [3:0] OpCode,
  output Mem_Read
);

  wire and_1_out, and_2_out, not_1_out;

  not not_1 (not_1_out, OpCode[2]);
  and and_1 (and_1_out, OpCode[3], not_1_out);
  and and_2 (and_2_out, OpCode[1], OpCode[0]);
  and and_3 (Mem_Read, and_1_out, and_2_out);
endmodule

module MemWrite (
  input  [3:0] OpCode,
  output Mem_Write
);

  wire and_1_out, and_2_out, not_1_out, not_2_out;

  not not_1 (not_1_out, OpCode[2]);
  not not_2 (not_2_out, OpCode[0]);
  and and_1 (and_1_out, OpCode[3], not_1_out);
  and and_2 (and_2_out, OpCode[1], not_2_out);
  and and_3 (Mem_Write, and_1_out, and_2_out);
endmodule

module Branch (
  input  [3:0] OpCode,
  output Branch_Out
);

  wire and_1_out, not_1_out, not_2_out;

  not not_1 (not_1_out, OpCode[3]);
  and and_1 (and_1_out, not_1_out, OpCode[2]);
  not not_2 (not_2_out, OpCode[1]);
  and and_2 (Branch_Out, and_1_out, not_2_out);
endmodule

module Register_File (
  input  W,
  input  [2:0] read2,
  input  [2:0] read1,
  input  [2:0] reg_W,
  input  [15:0] d_W,
  input  clk,
  input  reset,
  output [15:0] d1,
  output [15:0] d2
);

  wire and_1_out, and_2_out, and_3_out, and_4_out, and_5_out, and_6_out, and_7_out, and_8_out,
       decoder_1_out0, decoder_1_out1, decoder_1_out2, decoder_1_out3, decoder_1_out4, decoder_1_out5,
       decoder_1_out6, decoder_1_out7;
  wire [15:0] r1_q, r2_q, r3_q, r4_q, r5_q, r6_q, r7_q, r8_q;

  Decoder #(.enable("false"), .select(3)) decoder_1 (
    .out0(decoder_1_out0), .out1(decoder_1_out1), .out2(decoder_1_out2), .out3(decoder_1_out3),
    .out4(decoder_1_out4), .out5(decoder_1_out5), .out6(decoder_1_out6), .out7(decoder_1_out7), .sel(reg_W));
  and and_1 (and_1_out, W, decoder_1_out0);
  and and_2 (and_2_out, W, decoder_1_out1);
  and and_3 (and_3_out, W, decoder_1_out2);
  and and_4 (and_4_out, W, decoder_1_out3);
  and and_5 (and_5_out, W, decoder_1_out4);
  and and_6 (and_6_out, W, decoder_1_out5);
  and and_7 (and_7_out, W, decoder_1_out6);
  and and_8 (and_8_out, W, decoder_1_out7);
  Register #(.width(16)) r1 (.D(d_W), .en(and_1_out), .Q(r1_q), .clk(clk), .clr(reset));
  Register #(.width(16)) r2 (.D(d_W), .en(and_2_out), .Q(r2_q), .clk(clk), .clr(reset));
  Register #(.width(16)) r3 (.D(d_W), .en(and_3_out), .Q(r3_q), .clk(clk), .clr(reset));
  Register #(.trigger("falling"), .width(16)) r4 (.D(d_W), .en(and_4_out), .Q(r4_q), .clk(clk), .clr(reset));
  Register #(.width(16)) r5 (.D(d_W), .en(and_5_out), .Q(r5_q), .clk(clk), .clr(reset));
  Register #(.width(16)) r6 (.D(d_W), .en(and_6_out), .Q(r6_q), .clk(clk), .clr(reset));
  Register #(.width(16)) r7 (.D(d_W), .en(and_7_out), .Q(r7_q), .clk(clk), .clr(reset));
  Register #(.width(16)) r8 (.D(d_W), .en(and_8_out), .Q(r8_q), .clk(clk), .clr(reset));
  Multiplexer #(.enable("true"), .select(3), .width(16)) multiplexer_1 (
    .in0(r1_q), .in1(r2_q), .in2(r3_q), .in3(r4_q), .in4(r5_q), .in5(r6_q), .in6(r7_q), .in7(r8_q), .out(d2),
    .sel(read2));  // open: en
  Multiplexer #(.enable("true"), .select(3), .width(16)) multiplexer_2 (
    .in0(r1_q), .in1(r2_q), .in2(r3_q), .in3(r4_q), .in4(r5_q), .in5(r6_q), .in6(r7_q), .in7(r8_q), .out(d1),
    .sel(read1));  // open: en
endmodule

module ALUOp (
  input  [3:0] OpCode,
  output [1:0] ALU_Op
);

  wire and_1_out, and_2_out, and_3_out, and_4_out, and_5_out, and_6_out, and_7_out, and_8_out, and_9_out,
       and_10_out, and_11_out, and_12_out, and_13_out, and_14_out, and_15_out, and_16_out, not_1_out,
       not_2_out, not_3_out, not_4_out, not_5_out, not_6_out, not_7_out, not_8_out, or_2_out, or_3_out,
       or_4_out;

  and and_1 (and_1_out, OpCode[3], OpCode[2]);
  not not_1 (not_1_out, OpCode[3]);
  and and_2 (and_2_out, not_1_out, OpCode[2]);
  and and_3 (and_3_out, OpCode[3], not_2_out);
  not not_2 (not_2_out, OpCode[2]);
  and and_4 (and_4_out, OpCode[3], OpCode[1]);
  and and_5 (and_5_out, OpCode[3], not_3_out);
  not not_3 (not_3_out, OpCode[2]);
  and and_6 (and_6_out, OpCode[3], OpCode[2]);
  not not_4 (not_4_out, OpCode[1]);
  and and_7 (and_7_out, not_4_out, not_5_out);
  not not_5 (not_5_out, OpCode[0]);
  not not_6 (not_6_out, OpCode[3]);
  and and_8 (and_8_out, not_6_out, OpCode[2]);
  and and_9 (and_9_out, OpCode[1], not_7_out);
  not not_7 (not_7_out, OpCode[0]);
  not not_8 (not_8_out, OpCode[1]);
  and and_10 (and_10_out, and_1_out, not_8_out);
  and and_11 (and_11_out, and_2_out, OpCode[1]);
  and and_12 (and_12_out, and_3_out, OpCode[0]);
  and and_13 (and_13_out, and_4_out, OpCode[0]);
  and and_14 (and_14_out, and_5_out, OpCode[1]);
  and and_15 (and_15_out, and_6_out, and_7_out);
  and and_16 (and_16_out, and_8_out, and_9_out);
  or or_1 (ALU_Op[1], and_10_out, and_11_out);
  or or_2 (or_2_out, and_12_out, and_13_out);
  buf or_3 (or_3_out, and_15_out);  // OR_Gate
  or or_4 (or_4_out, or_2_out, or_3_out);
  or or_5 (ALU_Op[0], or_4_out, and_16_out);
endmodule

module Halt (
  input  [3:0] in_1,
  output Halt_Out
);

  wire or_1_out;

  or or_1 (or_1_out, in_1[3], in_1[2], in_1[1], in_1[0]);
  not not_1 (Halt_Out, or_1_out);
endmodule

module bne (
  input  [3:0] in_1,
  output bne_out
);

  wire and_1_out, and_2_out, not_1_out, not_2_out, not_3_out;

  not not_1 (not_1_out, in_1[3]);
  not not_2 (not_2_out, in_1[1]);
  not not_3 (not_3_out, in_1[0]);
  and and_1 (and_1_out, not_1_out, in_1[2]);
  and and_2 (and_2_out, not_2_out, not_3_out);
  and and_3 (bne_out, and_1_out, and_2_out);
endmodule

module BneBleHandler (
  input  [15:0] input1,
  input  [15:0] input2,
  input  bne_ble_state_1bne_0ble,
  output BNEBLE_out
);

  wire comparator_1_lt, comparator_2_eq, not_1_out;

  Comparator #(.width(16)) comparator_1 (.a(input1), .b(input2), .lt(comparator_1_lt));  // open: gt, eq
  Comparator #(.width(16)) comparator_2 (.a(input1), .b(input2), .eq(comparator_2_eq));  // open: gt, lt
  not not_1 (not_1_out, comparator_2_eq);
  Multiplexer #(.enable("true")) multiplexer_1 (
    .in0(comparator_1_lt), .in1(not_1_out), .out(BNEBLE_out), .sel(bne_ble_state_1bne_0ble), .en(1'b1));
endmodule

module Jump (
  input  [3:0] OpCode,
  output Jump_out
);

  wire and_1_out, and_2_out, and_3_out, and_4_out, not_1_out, not_2_out, not_3_out, not_4_out;

  not not_1 (not_1_out, OpCode[3]);
  not not_2 (not_2_out, OpCode[2]);
  not not_3 (not_3_out, OpCode[3]);
  not not_4 (not_4_out, OpCode[2]);
  and and_1 (and_1_out, not_1_out, not_2_out);
  and and_2 (and_2_out, not_3_out, not_4_out);
  and and_3 (and_3_out, and_1_out, OpCode[0]);
  and and_4 (and_4_out, and_2_out, OpCode[1]);
  or or_1 (Jump_out, and_3_out, and_4_out);
endmodule

module Call (
  input  [3:0] in_1,
  output call_out
);

  wire and_1_out, and_2_out, and_3_out, not_1_out, not_2_out, not_3_out, not_4_out, not_5_out, not_6_out;

  not not_1 (not_1_out, in_1[3]);
  not not_2 (not_2_out, in_1[2]);
  not not_3 (not_3_out, in_1[0]);
  not not_4 (not_4_out, in_1[3]);
  not not_5 (not_5_out, in_1[2]);
  not not_6 (not_6_out, in_1[1]);
  and and_1 (and_1_out, not_1_out, not_2_out);
  and and_2 (and_2_out, in_1[1], not_3_out);
  and and_3 (and_3_out, not_4_out, not_5_out, not_6_out, in_1[0]);
  and and_4 (call_out, and_1_out, and_2_out);
endmodule

module Rtn (
  input  [3:0] in_1,
  output rtn_out
);

  wire and_1_out, and_2_out, not_1_out, not_2_out, not_3_out;

  not not_1 (not_1_out, in_1[3]);
  not not_2 (not_2_out, in_1[2]);
  not not_3 (not_3_out, in_1[1]);
  and and_1 (and_1_out, not_1_out, not_2_out);
  and and_2 (and_2_out, not_3_out, in_1[0]);
  and and_3 (rtn_out, and_1_out, and_2_out);
endmodule

module Move (
  input  [3:0] in_1,
  output move_out
);

  wire not_1_out, not_2_out, not_3_out;

  not not_1 (not_1_out, in_1[2]);
  and and_1 (move_out, in_1[3], not_1_out, not_2_out, in_1[0]);
  not not_2 (not_2_out, in_1[1]);
  not not_3 (not_3_out, in_1[2]);
  // AND_Gate and_2 has open pins: in0=in_1[3], in1=not_3_out, in2=in_1[1], in3=in_1[0], out=open
endmodule
